# Fritzing sketch PCB Design (saved by Fritzing 0.9.10b)
circuit board: 8.61953cm x 6.07012cm
breadboards: 1

parts:
  Vin = Pad [width=1.9990740740740687 height=3.5512962962962953 connect=center]
  GND = Pad [width=3.668888888888888 height=3.8099999999999996 connect=center]
  Vin_2 = Pad [width=3.668888888888888 height=3.8099999999999996 connect=center]
  Din = Pad [width=1.9990740740740687 height=3.5512962962962953 connect=center]
  GND_2 = Pad [width=1.9990740740740687 height=3.5512962962962953 connect=center]
  GND1 = Pad [width=4.402666666666673 height=1.721555555555554 connect=center]
  Vin1 = Pad [width=4.12044444444445 height=1.721555555555554 connect=center]
  R2 = Resistor [tolerance=±5% power=0.25 resistance=220k package=THT]
  R1 = Resistor [tolerance=±5% power=0.25 resistance=200k package=THT]
  PCM5102A = PCM5102A I2S Stereo DAC
  C3 = Ceramic Capacitor [capacitance=100nF voltage=35V package="100 mil [THT, multilayer]"]
  C2 = Ceramic Capacitor [capacitance=33pF voltage=35V package="100 mil [THT, multilayer]"]
  R3 = Resistor [tolerance=±5% power=0.25 resistance=220k package=THT]
  C1 = Ceramic Capacitor [capacitance=100nF voltage=35V package="100 mil [THT, multilayer]"]
  MSGEQ = MSGEQ7 Chip [package=THT]
  C4 = Ceramic Capacitor [capacitance=100nF voltage=35V package="100 mil [THT, multilayer]"]
  ESP32 = LuaNode32 / ESP32 [part_number=ESP32S-PIN30]
  ESP32C3 = seeeduino-xiao

nets:
  N1: Vin.pad, Vin_2.pad, Vin1.pad, ESP32.Vin
  GND: GND.pad, GND_2.pad, GND1.pad, PCM5102A.GND, ESP32.GND
  N2: Din.pad, ESP32C3.D7
  N3: R2.Pin_0, PCM5102A.LROUT
  N4: R2.Pin_1, R3.Pin_1, C4.1
  VDD: R1.Pin_0, C1.0, MSGEQ.VDD, ESP32C3.5V
  N5: R1.Pin_1, C2.0, MSGEQ.CKIN
  N6: PCM5102A.ROUT, R3.Pin_0
  VSS: PCM5102A.AGND, C3.1, C2.1, C1.1, MSGEQ.VSS, ESP32C3.GND
  N7: PCM5102A.BCK, ESP32.D26
  N8: PCM5102A.DIN, ESP32.D22
  N9: PCM5102A.LRCK, ESP32.D25
  VIN: PCM5102A.VIN, ESP32.3V3
  N10: C3.0, MSGEQ.GND
  N11: MSGEQ.OUT, ESP32C3.D0
  N12: MSGEQ.STROBE, ESP32C3.D1
  N13: MSGEQ.IN, C4.0
  N14: MSGEQ.RESET, ESP32C3.D2

custom parts:
  MSGEQ7 Chip: Seven Band Graphic Equalizer
  LuaNode32 / ESP32: New Image for LuaNode32 DOIT ESP32 DEVKIT V1. Base parts from LuaNode32 / ESP32 ESP32 based LuaNode32 by G.Noorlander DOIT Esp32 DevKit v1 (30 pins long, 11 pins width) by Werner Rothschopf (modified by vanepp Dec 2018)
  seeeduino-xiao: Seeeduino XIAO processor board.
