# Fritzing sketch Schematic (saved by Fritzing 0.9.10b)

parts:
  C2 = Ceramic Capacitor [capacitance=33pF voltage=35V package="100 mil [THT, multilayer]"]
  R2 = Resistor [tolerance=±5% resistance=220k package="0805 [SMD]"]
  MSGEQ7 = IC, DIP package, 8 pins [chip_label=IC]
  C3 = Ceramic Capacitor [capacitance=100nF voltage=35V package="100 mil [THT, multilayer]"]
  C1 = Ceramic Capacitor [capacitance=100nF voltage=35V package="100 mil [THT, multilayer]"]
  C4 = Ceramic Capacitor [capacitance=100nF voltage=35V package="100 mil [THT, multilayer]"]
  LED_Strip = WS2812 RGB LED strip
  R1 = Resistor [tolerance=±5% power=0.25 resistance=200k package=THT]
  R3 = Resistor [tolerance=±5% resistance=220k package="0805 [SMD]"]
  PCM5102A_I2S_Stereo_DAC2 = PCM5102A I2S Stereo DAC
  ESP32C3 = seeeduino-xiao
  ESP33 = LuaNode32 / ESP32 [part_number=ESP32S-PIN30]

nets:
  N1: C2.0, MSGEQ7.pin8
  N2: C2.1, MSGEQ7.pin2, C3.0, C1.0, PCM5102A_I2S_Stereo_DAC2.AGND, ESP32C3.GND
  N3: R2.Pin_0, PCM5102A_I2S_Stereo_DAC2.ROUT
  N4: R2.Pin_1, C4.1, R3.Pin_1
  N5: MSGEQ7.pin1, C1.1, R1.Pin_0, ESP32C3.5V
  N6: MSGEQ7.pin3, ESP32C3.D0
  N7: MSGEQ7.pin4, ESP32C3.D1
  N8: MSGEQ7.pin5, C4.0
  N9: MSGEQ7.pin6, C3.1
  N10: MSGEQ7.pin7, ESP32C3.D2
  N11: LED_Strip.DIN, ESP32C3.D7
  N12: R3.Pin_0, PCM5102A_I2S_Stereo_DAC2.LROUT
  N13: PCM5102A_I2S_Stereo_DAC2.BCK, ESP33.D26
  N14: PCM5102A_I2S_Stereo_DAC2.DIN, ESP33.D22
  N15: PCM5102A_I2S_Stereo_DAC2.LRCK, ESP33.D25
  GND: PCM5102A_I2S_Stereo_DAC2.GND, ESP33.GND
  VIN: PCM5102A_I2S_Stereo_DAC2.VIN, ESP33.3V3

notes:
  ESP32S,ESP32 and WSB2812 share the same 5V power supply(schematic does not provide Vin + GND pins for ESP)

custom parts:
  WS2812 RGB LED strip: WS2812 strip
  seeeduino-xiao: Seeeduino XIAO processor board.
  LuaNode32 / ESP32: New Image for LuaNode32 DOIT ESP32 DEVKIT V1. Base parts from LuaNode32 / ESP32 ESP32 based LuaNode32 by G.Noorlander DOIT Esp32 DevKit v1 (30 pins long, 11 pins width) by Werner Rothschopf (modified by vanepp Dec 2018)
